# Fritzing sketch ElectricScheme_PISmartRobot27 (saved by Fritzing 1.0.1rc)

parts:
  RaspberryPi = Raspberry Pi 4B
  L293D = L293D [package=THT]
  M2 = DC Motor [voltage_(max)=6V voltage_(min)=3V]
  M1 = DC Motor [voltage_(max)=6V voltage_(min)=3V]
  Emitter/Sensor_Ultrasons = HC-SR04 Ultrasonic Distance Sensor
  LineSensor1 = Grove Light Sensor
  LineSensor2 = Grove Light Sensor
  switch = Round Pushbutton
  LineSensor3 = Grove Light Sensor
  Battery = Battery
  WAGO_Alim_Moteur = Camdenboss CTB0158-3 [part_number=CTB0158-3 package=THT]
  LCD1 = LCD screen
  WAGO_GND_SON = Camdenboss CTB0158-3 [part_number=CTB0158-3 package=THT]
  Buzzer = Piezo Speaker
  WAGO_GND_Capteurs/LCD = Camdenboss CTB0158-5 [part_number=CTB0158-5 package=THT]
  WAGO_Alim_Moteur3 = Camdenboss CTB0158-5 [part_number=CTB0158-5 package=THT]
  LCM1602_IIC1 = LCM1602 IIC [part_number="LCM1602 IIC" chip_label="LCM1602 IIC" package="DIP (Dual Inline) [THT]"]
  LED1 = smd LED [color="Red (633nm)" package="1206 [SMD]"]
  R1 = Resistor [tolerance=±5% power=0.25 resistance=220 package=THT]

nets:
  3V3: RaspberryPi.3V3, Emitter/Sensor_Ultrasons.VCC
  N1: RaspberryPi.5V, WAGO_Alim_Moteur3.terminal_5
  N2: RaspberryPi.GPIO2, LCM1602_IIC1.SDA
  N3: RaspberryPi.GPIO3, LCM1602_IIC1.SCL
  N4: RaspberryPi.GND, L293D.0V, Battery.-, WAGO_GND_SON.terminal_2, WAGO_GND_Capteurs/LCD.terminal_5
  N5: RaspberryPi.GPIO4, Emitter/Sensor_Ultrasons.TRIG
  N6: RaspberryPi.GPIO14, L293D.In_3
  N7: RaspberryPi.GPIO15, L293D.In_4
  N8: RaspberryPi.GPIO25, LineSensor3.SIG
  N9: RaspberryPi.GPIO8, LineSensor2.SIG
  N10: RaspberryPi.GPIO7, LineSensor1.SIG
  N11: RaspberryPi.GPIO5, Emitter/Sensor_Ultrasons.ECHO
  N12: RaspberryPi.GPIO12, L293D.Enable_2
  N13: RaspberryPi.GPIO13, L293D.Enable_1
  N14: RaspberryPi.GPIO16, Buzzer.pin2
  N15: RaspberryPi.GPIO20, L293D.In_1
  N16: RaspberryPi.GPIO21, L293D.In_2
  N17: L293D.Out_1_(_Controlled_by_Enable_1_), M1.pin_2
  N18: L293D.Out_2_(_Controlled_by_Enable_1_), M1.pin_1
  N19: L293D.+Vmotor, LED1.cathode
  N20: L293D.Out_3_(_Controlled_by_Enable_2_), M2.pin_2
  N21: L293D.Out_4_(_Controlled_by_Enable_2_), M2.pin_1
  N22: L293D.+V, WAGO_Alim_Moteur.terminal_3
  N23: Emitter/Sensor_Ultrasons.GND, WAGO_GND_SON.terminal_1
  N24: LineSensor1.GND, WAGO_GND_Capteurs/LCD.terminal_1
  N25: LineSensor1.VCC, WAGO_Alim_Moteur3.terminal_1
  N26: LineSensor2.GND, WAGO_GND_Capteurs/LCD.terminal_2
  N27: LineSensor2.VCC, WAGO_Alim_Moteur3.terminal_2
  N28: switch.leg0, WAGO_Alim_Moteur.terminal_2
  N29: switch.leg1, R1.Pin_0
  N30: LineSensor3.GND, WAGO_GND_Capteurs/LCD.terminal_3
  N31: LineSensor3.VCC, WAGO_Alim_Moteur3.terminal_3
  N32: Battery.+, WAGO_Alim_Moteur.terminal_1
  VSS: LCD1.VSS, LCM1602_IIC1.VSS
  VDD: LCD1.VDD, LCM1602_IIC1.VDD
  N33: LCD1.V0, LCM1602_IIC1.V0
  N34: LCD1.RS, LCM1602_IIC1.RS
  N35: LCD1.R/W, LCM1602_IIC1.RW
  N36: LCD1.E, LCM1602_IIC1.E
  N37: LCD1.DB0, LCM1602_IIC1.D0
  N38: LCD1.DB1, LCM1602_IIC1.D1
  N39: LCD1.DB2, LCM1602_IIC1.D2
  N40: LCD1.DB3, LCM1602_IIC1.D3
  N41: LCD1.DB4, LCM1602_IIC1.D4
  N42: LCD1.DB5, LCM1602_IIC1.D5
  N43: LCD1.DB6, LCM1602_IIC1.D6
  N44: LCD1.DB7, LCM1602_IIC1.D7
  N45: LCD1.LED+, LCM1602_IIC1.A
  N46: LCD1.LED-, LCM1602_IIC1.K
  N47: WAGO_GND_SON.terminal_3, Buzzer.pin1
  N48: WAGO_GND_Capteurs/LCD.terminal_4, LCM1602_IIC1.GND
  N49: WAGO_Alim_Moteur3.terminal_4, LCM1602_IIC1.VCC
  N50: LED1.anode, R1.Pin_1

notes:
  Grove light sensor (<=> capteurs de ligne)
  Emetteur/capteur Ultrasons
  Trig : GPIO 4
  Echo : GPIO 5
  L293D avec Moteurs
  EN1 GPIO 13
  EN2 GPIO 12
  M1
  In 1 : GPIO 20
  In 2 : GPIO 21
  M2
  In 3 : GPIO 14
  In 4 : GPIO 15
  Speaker
  GPIO 16
  Interrupteur et LED
  capteurs de déviation:
  GPIO 7
  GPIO 8
  Capteur de fin de ligne
  GPIO 25
  Wago GND Capteur/LCD
  Batteries NIMH 2*3.7V
  Wago Alim Moteur
  Ecran LCD
  LCM 1602 IIC
  SDA : GPIO 2
  SCL : GPIO 3
  Wago GND SON
  Wago 5V Capteur/LCD
  Ici la LED doit être montée en parallèle

custom parts:
  LCM1602 IIC: I2C-Module to use a 1602 or 2004 LCD on with the wire.h libory Serial LCD Modul
